# Fritzing sketch Instrument (saved by Fritzing 0.9.4)
breadboards: 1

parts:
  Part1 = Arduino Uno (Rev3)
  Part2 = Thumb Joystick
  J1 = Piezo Speaker
  S1 = Pushbutton [package="[THT]"]
  S2 = Pushbutton [package="[THT]"]
  S3 = Pushbutton [package="[THT]"]
  S4 = Pushbutton [package="[THT]"]
  R1 = Trimmer Potentiometer [maximum_resistance=10kΩ package=THT]
  LCD1 = LCD screen
  R2 = Trimmer Potentiometer [maximum_resistance=10kΩ package=THT]

nets:
  N1: Part1.A0, Part2.VERT
  N2: Part1.A1, Part2.HORZ
  N3: Part1.D8, S1.Pin_1, S1.Pin_2
  N4: Part1.D9_PWM, S2.Pin_1, S2.Pin_2
  N5: Part1.D10_PWM/SS, S3.Pin_1, S3.Pin_2
  N6: Part1.D11_PWM/MOSI, LCD1.R/W
  N7: Part1.D12/MISO, LCD1.RS
  N8: Part1.D2, LCD1.DB7
  N9: Part1.D3_PWM, LCD1.DB6
  N10: Part1.D4, LCD1.DB5
  N11: Part1.D5_PWM, LCD1.DB4
  N12: Part1.D7, J1.pin2, R1.wiper
  5V: Part1.5V, Part2.VCC, R1.leg1, LCD1.VDD, LCD1.LED+, R2.leg1
  GND: Part1.GND, Part2.GND, J1.pin1, S1.Pin_3, S1.Pin_4, S2.Pin_3, S2.Pin_4, S3.Pin_3, S3.Pin_4, S4.Pin_3, S4.Pin_4, R1.leg2, LCD1.VSS, LCD1.LED-, R2.leg2
  N13: S4.Pin_1, S4.Pin_2
  N14: LCD1.V0, R2.wiper
